# Fritzing sketch no-overflow-sketch (saved by Fritzing 0.9.3b)

parts:
  Part1 = Adafruit Trinket M0 [part_number="Adafruit #3500"]
  Part2 = Adafruit Micro USB Breakout [part_number="Adafruit #1833"]
  J1 = Piezo Speaker
  X1 = USB Connectors [package=usb-a-s-nosilk]
  U1 = POT [package=pot_mammoth]
  J2 = Power Jack [package=power_jack_pth_lock]
  Q1 = TIP120 Hi-Current Darlington Transistor

nets:
  N1: Part1.VBAT, Part2.VBUS
  GND: Part1.GND, Part2.GND, Part2.D-, J1.pin1, U1.E
  N2: Part1.D4_A2_PA06_TXD_MOSI, J1.pin2
  N3: Part1.D3_A3_PA07_RXD_SCK, Part2.D+
  N4: Part1.3.3V, U1.A
  N5: Part1.D0_A4_PA08_SDA, U1.S
  N6: X1.D+, Q1.BASE
  GND_2: X1.GND, J2.GND
  N7: X1.VBUS, J2.PWR

notes:
  Power and switching signal sent to Digital Loggers IoT Power Relay
  https://www.adafruit.com/product/2935
  Potentiometer is a Milone 5" enclosed eTape liquid level sensor
  https://www.adafruit.com/product/3828

custom parts:
  Adafruit Micro USB Breakout: Simple but effective - this breakout board has a USB Micro-B connector, with all 5 pins broken out. Great for pairing with a microcontroller with USB support, or adding USB 5V power to a project. We use a micro-AB connector with through-hole shielding pads for an excellent strong connection - it won't rip off by accident! Comes with one fully assembled and tested micro B breakout PCB and a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
